# Fritzing sketch waterbot (saved by Fritzing 0.9.10b)

parts:
  Photon = Photon
  Button = Pushbutton [package=THT]
  Meter = Reed switch [package=THT]

nets:
  N1: Photon.GND, Photon.VBAT, Button.leg1, Meter.pin_2
  N2: Photon.D2, Meter.pin_1
  N3: Photon.RST, Button.leg0
